// Digital circuit somador_avx.dig as structural Verilog
module somador_avx (
  input  in_1,
  input  [31:0] in_2,
  input  [1:0] in_3,
  input  [31:0] in_4,
  output [31:0] out_5
);

  Somador_Subtrator_Vetorial #(.applicationType("GHDL"), .CodeFile("C:\\Users\\igorv\\OneDrive\\Área de Trabalho\\Universidade\\arqcomp\\Somador_Subtrator_Vetorial.vhd")) u_Somador_Subtrator_Vetorial (
    .A_i(in_4), .B_i(in_2), .mode_i(in_1), .vecSize_i(in_3), .S_o(out_5));
endmodule
