// Digital circuit CPU_RISCV_VEC.dig as structural Verilog
module CPU_RISCV_VEC (
  input  clk,
  input  [31:0] Entrada,
  input  in_3
);

  wire and_1_out, and_2_out, and_3_out, multiplexer_8_out, not_1_out, or_1_out, u_Control_alusrc,
       u_Control_branch, u_Control_jumpreg, u_Control_memread, u_Control_memtoreg, u_Control_memwrite,
       u_Control_pc_shift_ctrl, u_Control_regwrite, u_exmem_branch, u_exmem_jar, u_exmem_memread,
       u_exmem_memtoreg, u_exmem_memwrite, u_exmem_regwrite, u_exmem_zero_flag, u_Hazerd_stall,
       u_idex_aluscr, u_idex_branch, u_idex_jumpreg, u_idex_memread, u_idex_memtoreg, u_idex_memwrite,
       u_idex_pc_shift_ctrl, u_idex_regwrite, u_memwb_memtoreg, u_memwb_regwrite, u_ULA_control_beq_ben,
       u_ULA_zero_flag, u_vector_is32, u_vector_zero_flag;
  wire [1:0] u_Control_aluop, u_Forward_forward1, u_Forward_forward2, u_idex_aluop, u_ULA_control_vecsize;
  wire [2:0] u_Control_funct3, u_idex_funct3;
  wire [3:0] u_ULA_control_alu_ctrl, u_vector_control_out;
  wire [4:0] u_exmem_regaddrd, u_idex_regaddr1, u_idex_regaddr2, u_idex_regaddrd, u_instr_fetch_regaddr1,
       u_instr_fetch_regaddr2, u_instr_fetch_regaddrw, u_memwb_regaddrd;
  wire [6:0] u_Control_funct7, u_Control_opcode, u_idex_funct7, u_idex_opcode;
  wire [15:0] ramdualport_1_d, ramdualport_2_d, u_spliter_2_data_out1, u_spliter_2_data_out2,
       u_spliter_data_out1, u_spliter_data_out2;
  wire [31:0] multiplexer_1_out, multiplexer_2_out, multiplexer_3_out, multiplexer_4_out, multiplexer_5_out,
       multiplexer_6_out, multiplexer_7_out, multiplexer_9_out, multiplexer_10_out, Registers_da,
       Registers_db, u_adder_sum, u_exmem_alures, u_exmem_db, u_exmem_pc2, u_idex_da, u_idex_db, u_idex_imm,
       u_idex_pc, u_ImmGen_imm, u_instr_fetch_inst_out, u_instr_fetch_pc_next_out, u_instr_fetch_pc_out,
       u_joiner_data_out, u_memwb_alures, u_memwb_memdata, u_PC_pc_out, u_ULA_result, u_vector_entry1_out,
       u_vector_entry2_out, u_vector_result;

  Multiplexer #(.Bits(32)) multiplexer_1 (
    .sel(or_1_out), .in_0(u_PC_pc_out), .in_1(u_exmem_pc2), .out(multiplexer_1_out));
  PC #(.applicationType("GHDL"), .CodeFile("C:\\Users\\igorv\\OneDrive\\Área de Trabalho\\Universidade\\arqcomp\\cpu_riscv_vec\\PC.vhd")) u_PC (
    .clk(clk), .reset(in_3), .PC_in(multiplexer_1_out), .PC_write(not_1_out), .PC_out(u_PC_pc_out));
  instr_fetch #(.applicationType("GHDL"), .CodeFile("C:\\Users\\igorv\\OneDrive\\Área de Trabalho\\Universidade\\arqcomp\\cpu_riscv_vec\\instr_fetch.vhd")) u_instr_fetch (
    .clk(clk), .PC_write(not_1_out), .PC_in(u_PC_pc_out), .PC_next_in(u_instr_fetch_pc_next_out),
    .Inst_in(Entrada), .PC_out(u_instr_fetch_pc_out), .PC_next_out(u_instr_fetch_pc_next_out),
    .Inst_out(u_instr_fetch_inst_out), .RegAddr1(u_instr_fetch_regaddr1), .RegAddr2(u_instr_fetch_regaddr2),
    .RegAddrW(u_instr_fetch_regaddrw));
  Hazerd #(.applicationType("GHDL"), .CodeFile("C:\\Users\\igorv\\OneDrive\\Área de Trabalho\\Universidade\\arqcomp\\cpu_riscv_vec\\Hazard.vhd")) u_Hazerd (
    .clk(clk), .MemRead(u_Control_memtoreg), .RegAddr1(u_instr_fetch_regaddr1),
    .RegAddr2(u_instr_fetch_regaddr2), .RegAddrD(u_idex_regaddrd), .stall(u_Hazerd_stall));
  not not_1 (not_1_out, u_Hazerd_stall);
  Control #(.applicationType("GHDL"), .CodeFile("C:\\Users\\igorv\\OneDrive\\Área de Trabalho\\Universidade\\arqcomp\\cpu_riscv_vec\\Control.vhd")) u_Control (
    .instr(u_instr_fetch_inst_out), .stall(u_Hazerd_stall), .Branch(u_Control_branch),
    .MemRead(u_Control_memread), .MemtoReg(u_Control_memtoreg), .ALUop(u_Control_aluop),
    .MemWrite(u_Control_memwrite), .ALUsrc(u_Control_alusrc), .RegWrite(u_Control_regwrite),
    .funct7(u_Control_funct7), .funct3(u_Control_funct3), .opcode(u_Control_opcode),
    .PC_shift_ctrl(u_Control_pc_shift_ctrl), .JumpReg(u_Control_jumpreg));
  RegisterFile #(.AddrBits(5), .Bits(32)) Registers (
    .Din(multiplexer_10_out), .we(u_memwb_regwrite), .Rw(u_memwb_regaddrd), .C(clk),
    .Ra(u_instr_fetch_regaddr1), .Rb(u_instr_fetch_regaddr2), .Da(Registers_da), .Db(Registers_db));
  ImmGen #(.applicationType("GHDL"), .CodeFile("C:\\Users\\igorv\\OneDrive\\Área de Trabalho\\Universidade\\arqcomp\\cpu_riscv_vec\\ImmGen.vhd")) u_ImmGen (
    .instr(u_instr_fetch_inst_out), .imm(u_ImmGen_imm));
  idex #(.applicationType("GHDL"), .CodeFile("C:\\Users\\igorv\\OneDrive\\Área de Trabalho\\Universidade\\arqcomp\\cpu_riscv_vec\\idex.vhd")) u_idex (
    .clk(clk), .Branch_in(u_Control_branch), .MemRead_in(u_Control_memread),
    .MemtoReg_in(u_Control_memtoreg), .ALUop_in(u_Control_aluop), .MemWrite_in(u_Control_memwrite),
    .ALUscr_in(u_Control_alusrc), .RegWrite_in(u_Control_regwrite), .funct7_in(u_Control_funct7),
    .funct3_in(u_Control_funct3), .opcode_in(u_Control_opcode), .PC_shift_ctrl_in(u_Control_pc_shift_ctrl),
    .JumpReg_in(u_Control_jumpreg), .PC_in(u_instr_fetch_pc_out), .Da_in(Registers_da), .Db_in(Registers_db),
    .imm_in(u_ImmGen_imm), .RegAddr1_in(u_instr_fetch_regaddr1), .RegAddr2_in(u_instr_fetch_regaddr2),
    .RegAddrD_in(u_instr_fetch_regaddrw), .Branch(u_idex_branch), .MemRead(u_idex_memread),
    .MemtoReg(u_idex_memtoreg), .ALUop(u_idex_aluop), .MemWrite(u_idex_memwrite), .ALUscr(u_idex_aluscr),
    .RegWrite(u_idex_regwrite), .funct7(u_idex_funct7), .funct3(u_idex_funct3), .opcode(u_idex_opcode),
    .PC_shift_ctrl(u_idex_pc_shift_ctrl), .JumpReg(u_idex_jumpreg), .PC(u_idex_pc), .Da(u_idex_da),
    .Db(u_idex_db), .imm(u_idex_imm), .RegAddr1(u_idex_regaddr1), .RegAddr2(u_idex_regaddr2),
    .RegAddrD(u_idex_regaddrd));
  Forward #(.applicationType("GHDL"), .CodeFile("C:\\Users\\igorv\\OneDrive\\Área de Trabalho\\Universidade\\arqcomp\\cpu_riscv_vec\\Forward.vhd")) u_Forward (
    .clk(clk), .WBregWrite(u_memwb_regwrite), .MEMregWrite(u_exmem_regwrite), .RegAddr1(u_idex_regaddr1),
    .RegAddr2(u_idex_regaddr2), .WBregD(u_memwb_regaddrd), .MEMregD(u_exmem_regaddrd),
    .Forward1(u_Forward_forward1), .Forward2(u_Forward_forward2));
  ULA_control #(.applicationType("GHDL"), .CodeFile("C:\\Users\\igorv\\OneDrive\\Área de Trabalho\\Universidade\\arqcomp\\cpu_riscv_vec\\ULA_control.vhd")) u_ULA_control (
    .funct7(u_idex_funct7), .funct3(u_idex_funct3), .opcode(u_idex_opcode), .ALUop(u_idex_aluop),
    .ALU_ctrl(u_ULA_control_alu_ctrl), .beq_ben(u_ULA_control_beq_ben), .VecSize(u_ULA_control_vecsize));
  and and_1 (and_1_out, u_idex_pc_shift_ctrl, ~u_idex_aluscr);  // And
  Multiplexer #(.Bits(32)) multiplexer_2 (
    .sel(u_idex_aluscr), .in_0(u_idex_db), .in_1(u_idex_imm), .out(multiplexer_2_out));
  Multiplexer #(.Bits(32)) multiplexer_3 (
    .sel(u_idex_jumpreg), .in_0(u_idex_pc), .in_1(u_idex_da), .out(multiplexer_3_out));
  Multiplexer #(.Bits(32)) multiplexer_4 (
    .sel(u_idex_pc_shift_ctrl), .in_0(u_idex_da), .in_1(u_idex_pc), .out(multiplexer_4_out));
  Multiplexer #(.Bits(32)) multiplexer_5 (
    .sel(and_1_out), .in_0(multiplexer_2_out), .in_1(32'h1), .out(multiplexer_5_out));
  adder #(.applicationType("GHDL"), .CodeFile("C:\\Users\\igorv\\OneDrive\\Área de Trabalho\\Universidade\\arqcomp\\cpu_riscv_vec\\adder.vhd")) u_adder (
    .Entry1(multiplexer_3_out), .Entry2(u_idex_imm), .Sum(u_adder_sum));
  Multiplexer #(.Selector_Bits(2), .Bits(32)) multiplexer_6 (
    .sel(u_Forward_forward2), .in_0(multiplexer_5_out), .in_1(multiplexer_10_out), .in_2(u_exmem_alures),
    .in_3({32{1'b0}}), .out(multiplexer_6_out));
  Multiplexer #(.Selector_Bits(2), .Bits(32)) multiplexer_7 (
    .sel(u_Forward_forward1), .in_0(multiplexer_4_out), .in_1(multiplexer_10_out), .in_2(u_exmem_alures),
    .in_3({32{1'b0}}), .out(multiplexer_7_out));
  vector #(.applicationType("GHDL"), .CodeFile("C:\\Users\\igorv\\OneDrive\\Área de Trabalho\\Universidade\\arqcomp\\cpu_riscv_vec\\vector.vhd")) u_vector (
    .Entry1(multiplexer_7_out), .Entry2(multiplexer_6_out), .control(u_ULA_control_alu_ctrl),
    .VecSize(u_ULA_control_vecsize), .Entry1_out(u_vector_entry1_out), .Entry2_out(u_vector_entry2_out),
    .control_out(u_vector_control_out), .result(u_vector_result), .zero_flag(u_vector_zero_flag),
    .is32(u_vector_is32));
  ULA #(.applicationType("GHDL"), .CodeFile("C:\\Users\\igorv\\OneDrive\\Área de Trabalho\\Universidade\\arqcomp\\cpu_riscv_vec\\ULA.vhd")) u_ULA (
    .Entry1(u_vector_entry1_out), .Entry2(u_vector_entry2_out), .control(u_vector_control_out),
    .result(u_ULA_result), .zero_flag(u_ULA_zero_flag));
  Multiplexer multiplexer_8 (
    .sel(u_vector_is32), .in_0(u_ULA_zero_flag), .in_1(u_vector_zero_flag), .out(multiplexer_8_out));
  Multiplexer #(.Bits(32)) multiplexer_9 (
    .sel(u_vector_is32), .in_0(u_ULA_result), .in_1(u_vector_result), .out(multiplexer_9_out));
  and and_2 (and_2_out, u_ULA_control_beq_ben, multiplexer_8_out);
  exmem #(.applicationType("GHDL"), .CodeFile("C:\\Users\\igorv\\OneDrive\\Área de Trabalho\\Universidade\\arqcomp\\cpu_riscv_vec\\exmem.vhd")) u_exmem (
    .clk(clk), .Branch_in(u_idex_branch), .MemRead_in(u_idex_memread), .MemtoReg_in(u_idex_memtoreg),
    .MemWrite_in(u_idex_memwrite), .RegWrite_in(u_idex_regwrite), .PC2_in(u_adder_sum), .Db_in(u_idex_db),
    .RegAddrD_in(u_idex_regaddrd), .zero_flag_in(and_2_out), .ALUres_in(multiplexer_9_out),
    .jar_in(and_1_out), .Branch(u_exmem_branch), .MemRead(u_exmem_memread), .MemtoReg(u_exmem_memtoreg),
    .MemWrite(u_exmem_memwrite), .RegWrite(u_exmem_regwrite), .PC2(u_exmem_pc2), .Db(u_exmem_db),
    .RegAddrD(u_exmem_regaddrd), .zero_flag(u_exmem_zero_flag), .ALUres(u_exmem_alures), .jar(u_exmem_jar));
  and and_3 (and_3_out, u_exmem_branch, u_exmem_zero_flag);
  or or_1 (or_1_out, and_3_out, u_exmem_jar);
  spliter #(.applicationType("GHDL"), .CodeFile("C:\\Users\\igorv\\OneDrive\\Área de Trabalho\\Universidade\\arqcomp\\cpu_riscv_vec\\spliter.vhd")) u_spliter (
    .data_in(u_exmem_db), .data_out1(u_spliter_data_out1), .data_out2(u_spliter_data_out2));
  spliter #(.applicationType("GHDL"), .CodeFile("C:\\Users\\igorv\\OneDrive\\Área de Trabalho\\Universidade\\arqcomp\\cpu_riscv_vec\\spliter.vhd")) u_spliter_2 (
    .data_in(u_exmem_alures), .data_out1(u_spliter_2_data_out1), .data_out2(u_spliter_2_data_out2));
  RAMDualPort #(.AddrBits(16), .Bits(16)) ramdualport_1 (
    .A(u_spliter_data_out1), .Din(u_spliter_2_data_out1), .str(u_exmem_memwrite), .C(clk),
    .ld(u_exmem_memread), .D(ramdualport_1_d));
  RAMDualPort #(.AddrBits(16), .Bits(16)) ramdualport_2 (
    .A(u_spliter_data_out2), .Din(u_spliter_2_data_out2), .str(u_exmem_memwrite), .C(clk),
    .ld(u_exmem_memread), .D(ramdualport_2_d));
  joiner #(.applicationType("GHDL"), .CodeFile("C:\\Users\\igorv\\OneDrive\\Área de Trabalho\\Universidade\\arqcomp\\cpu_riscv_vec\\joiner.vhd")) u_joiner (
    .data_in1(ramdualport_1_d), .data_in2(ramdualport_2_d), .data_out(u_joiner_data_out));
  memwb #(.applicationType("GHDL"), .CodeFile("C:\\Users\\igorv\\OneDrive\\Área de Trabalho\\Universidade\\arqcomp\\cpu_riscv_vec\\memwb.vhd")) u_memwb (
    .clk(clk), .RegWrite_in(u_exmem_regwrite), .MemtoReg_in(u_exmem_memtoreg),
    .MemData_in(u_joiner_data_out), .ALUres_in(u_exmem_alures), .RegAddrD_in(u_exmem_regaddrd),
    .RegWrite(u_memwb_regwrite), .MemtoReg(u_memwb_memtoreg), .MemData(u_memwb_memdata),
    .ALUres(u_memwb_alures), .RegAddrD(u_memwb_regaddrd));
  Multiplexer #(.Bits(32)) multiplexer_10 (
    .sel(u_memwb_memtoreg), .in_0(u_memwb_alures), .in_1(u_memwb_memdata), .out(multiplexer_10_out));
endmodule
