// Logisim project Trabalho_IV.circ as structural Verilog
module main (
  input  in_1
);

  wire alu_1_f_zero, alu_control_1_beq_bne, and_1_out, and_2_out, and_3_out, clock_1_out,
       control_unit_1_alusrc, control_unit_1_branch, control_unit_1_jumpreg, control_unit_1_memread,
       control_unit_1_memtoreg, control_unit_1_memwrite, control_unit_1_mode, control_unit_1_regwrite,
       control_unit_1_soma_pc, exmem_1_branch_out, exmem_1_jalr_ou_jal_out, exmem_1_memread_out,
       exmem_1_memtoreg_out, exmem_1_memwrite_out, exmem_1_regwrite_out, exmem_1_zero_out, hazard_1_stall,
       idex_1_alusrc_out, idex_1_branch_out, idex_1_jumpreg_out, idex_1_memread_out, idex_1_memtoreg_out,
       idex_1_memwrite_out, idex_1_mode_out, idex_1_regwrite_out, idex_1_soma_pc_out, memwb_1_memtoreg_out,
       memwb_1_regwrite_out, not_1_out, not_2_out, or_1_out;
  wire [1:0] control_unit_1_aluop, control_unit_1_vecsize, forward_1_forwarda, forward_1_forwardb,
       idex_1_aluop_out, idex_1_vecsize_out;
  wire [2:0] control_unit_1_s_funct3, idex_1_funct3_out;
  wire [3:0] alu_control_1_alu_controle;
  wire [4:0] exmem_1_rd_out, idex_1_rd_out, idex_1_rs1_out, idex_1_rs2_out, ifid_1_rd, ifid_1_rs1,
       ifid_1_rs2, memwb_1_rd_out;
  wire [6:0] control_unit_1_s_funct7, control_unit_1_s_opcode, idex_1_funct7_out, idex_1_opcode_out;
  wire [23:0] exmem_1_aluresult_out;
  wire [31:0] alu_1_resultado, exmem_1_new_pc_out, exmem_1_read2_out, idex_1_immediate_out, idex_1_pc_out,
       idex_1_read1_out, idex_1_read2_out, ifid_1_instruction_out, ifid_1_pc_out, immgen_1_immediate,
       memwb_1_aluresult_out, memwb_1_mem_data_out, multiplexer_1_out, multiplexer_2_out, multiplexer_3_out,
       multiplexer_4_out, multiplexer_5_out, multiplexer_6_out, multiplexer_7_out, multiplexer_8_out,
       pc4_1_pc_out, ram_1_dout, registerfile_1_readdata_1, registerfile_1_readdata_2, rom_1_data,
       somador_1_z;
  wire [31:24] exmem_1_aluresult_out_2;

  Clock clock_1 (.out(clock_1_out));
  Multiplexer #(.enable("false"), .width(32)) multiplexer_1 (
    .in0(pc4_1_pc_out), .in1(exmem_1_new_pc_out), .out(multiplexer_1_out), .sel(or_1_out));
  PC4 pc4_1 (
    .CLK(clock_1_out), .RESET(in_1), .PC_in(multiplexer_1_out), .WriteEnable(not_1_out), .PC_out(pc4_1_pc_out));
  ROM #(.addrWidth(24), .dataWidth(32)) rom_1 (.addr(pc4_1_pc_out[23:0]), .data(rom_1_data));
  not not_1 (not_1_out, hazard_1_stall);
  IFID ifid_1 (
    .CLK(clock_1_out), .PC_in(pc4_1_pc_out), .WriteEnable(not_1_out), .Instruction_In(rom_1_data),
    .PC_out(ifid_1_pc_out), .Instruction_Out(ifid_1_instruction_out), .Rs1(ifid_1_rs1), .Rs2(ifid_1_rs2),
    .Rd(ifid_1_rd));  // open: PC4_in, PC4_out
  Control_Unit control_unit_1 (
    .instruction(ifid_1_instruction_out), .Stall(hazard_1_stall), .AluSrc(control_unit_1_alusrc),
    .RegWrite(control_unit_1_regwrite), .MemToReg(control_unit_1_memtoreg), .MemRead(control_unit_1_memread),
    .MemWrite(control_unit_1_memwrite), .Branch(control_unit_1_branch), .Soma_PC(control_unit_1_soma_pc),
    .AluOp(control_unit_1_aluop), .S_funct7(control_unit_1_s_funct7), .S_funct3(control_unit_1_s_funct3),
    .S_opcode(control_unit_1_s_opcode), .JumpReg(control_unit_1_jumpreg), .mode(control_unit_1_mode),
    .Vecsize(control_unit_1_vecsize));
  RegisterFile registerfile_1 (
    .ReadRegister_1(ifid_1_rs1), .ReadRegister_2(ifid_1_rs2), .WriteRegister(memwb_1_rd_out),
    .WriteData(multiplexer_8_out), .RegWrite(memwb_1_regwrite_out), .CLK(clock_1_out),
    .ReadData_1(registerfile_1_readdata_1), .ReadData_2(registerfile_1_readdata_2));
  ImmGen immgen_1 (.instruction(ifid_1_instruction_out), .immediate(immgen_1_immediate));
  Hazard hazard_1 (
    .clk(clock_1_out), .MemRead_in(idex_1_memread_out), .Rd_EX(idex_1_rd_out), .Rs1(ifid_1_rs1),
    .Rs2(ifid_1_rs2), .stall(hazard_1_stall));
  IDEX idex_1 (
    .CLK(clock_1_out), .ALUSrc_in(control_unit_1_alusrc), .ALUOp_in(control_unit_1_aluop),
    .funct3_in(control_unit_1_s_funct3), .funct7_in(control_unit_1_s_funct7), .PC_in(ifid_1_pc_out),
    .Soma_PC_in(control_unit_1_soma_pc), .Branch_in(control_unit_1_branch),
    .MemWrite_in(control_unit_1_memwrite), .MemRead_in(control_unit_1_memread),
    .RegWrite_in(control_unit_1_regwrite), .MemToReg_in(control_unit_1_memtoreg),
    .read1_in(registerfile_1_readdata_1), .read2_in(registerfile_1_readdata_2),
    .immediate_in(immgen_1_immediate), .Rd_in(ifid_1_rd), .Opcode_in(control_unit_1_s_opcode),
    .JumpReg_in(control_unit_1_jumpreg), .Rs1_In(ifid_1_rs1), .Rs2_In(ifid_1_rs2),
    .mode_in(control_unit_1_mode), .vecsize_in(control_unit_1_vecsize), .ALUSrc_out(idex_1_alusrc_out),
    .ALUOp_out(idex_1_aluop_out), .funct3_out(idex_1_funct3_out), .funct7_out(idex_1_funct7_out),
    .PC_out(idex_1_pc_out), .Soma_PC_out(idex_1_soma_pc_out), .Branch_out(idex_1_branch_out),
    .MemWrite_out(idex_1_memwrite_out), .MemRead_out(idex_1_memread_out), .RegWrite_out(idex_1_regwrite_out),
    .MemToReg_out(idex_1_memtoreg_out), .read1_out(idex_1_read1_out), .read2_out(idex_1_read2_out),
    .immediate_out(idex_1_immediate_out), .Rd_out(idex_1_rd_out), .Opcode_out(idex_1_opcode_out),
    .JumpReg_out(idex_1_jumpreg_out), .Rs1_out(idex_1_rs1_out), .Rs2_out(idex_1_rs2_out),
    .mode_out(idex_1_mode_out), .vecsize_out(idex_1_vecsize_out));
  not not_2 (not_2_out, idex_1_alusrc_out);
  and and_1 (and_1_out, not_2_out, idex_1_soma_pc_out);
  Multiplexer #(.enable("false"), .width(32)) multiplexer_2 (
    .in0(idex_1_read2_out), .in1(idex_1_immediate_out), .out(multiplexer_2_out), .sel(idex_1_alusrc_out));
  Multiplexer #(.enable("false"), .width(32)) multiplexer_3 (
    .in0(idex_1_pc_out), .in1(idex_1_read1_out), .out(multiplexer_3_out), .sel(idex_1_jumpreg_out));
  Multiplexer #(.enable("false"), .width(32)) multiplexer_4 (
    .in0(idex_1_read1_out), .in1(idex_1_pc_out), .out(multiplexer_4_out), .sel(idex_1_soma_pc_out));
  Multiplexer #(.enable("false"), .width(32)) multiplexer_5 (
    .in0(multiplexer_2_out), .in1(32'h1), .out(multiplexer_5_out), .sel(and_1_out));
  ALU_Control alu_control_1 (
    .Funct7(idex_1_funct7_out), .Funct3(idex_1_funct3_out), .Opcode(idex_1_opcode_out),
    .AluOp(idex_1_aluop_out), .ALU_Controle(alu_control_1_alu_controle), .Beq_Bne(alu_control_1_beq_bne));
  Multiplexer #(.enable("false"), .select(2), .width(32)) multiplexer_6 (
    .in0(multiplexer_4_out), .in1(multiplexer_8_out), .in2({exmem_1_aluresult_out_2, exmem_1_aluresult_out}),
    .out(multiplexer_6_out), .sel(forward_1_forwarda));  // open: in3
  Somador somador_1 (.A(multiplexer_3_out), .B(idex_1_immediate_out), .Z(somador_1_z));
  Multiplexer #(.enable("false"), .select(2), .width(32)) multiplexer_7 (
    .in0(multiplexer_5_out), .in1(multiplexer_8_out), .in2({exmem_1_aluresult_out_2, exmem_1_aluresult_out}),
    .out(multiplexer_7_out), .sel(forward_1_forwardb));  // open: in3
  ALU alu_1 (
    .A(multiplexer_6_out), .B(multiplexer_7_out), .controle(alu_control_1_alu_controle),
    .mode(idex_1_mode_out), .vecSize(idex_1_vecsize_out), .resultado(alu_1_resultado), .f_zero(alu_1_f_zero));
  Forward forward_1 (
    .clk(clock_1_out), .regWrite_WB(memwb_1_regwrite_out), .regWrite_MEM(exmem_1_regwrite_out),
    .Rs1(idex_1_rs1_out), .Rs2(idex_1_rs2_out), .Rd_WB(memwb_1_rd_out), .Rd_Mem(exmem_1_rd_out),
    .forwardA(forward_1_forwarda), .forwardB(forward_1_forwardb));
  and and_2 (and_2_out, alu_1_f_zero, alu_control_1_beq_bne);
  EXMEM exmem_1 (
    .CLK(clock_1_out), .Branch_in(idex_1_branch_out), .MemWrite_in(idex_1_memwrite_out),
    .MemRead_in(idex_1_memread_out), .RegWrite_in(idex_1_regwrite_out), .MemToReg_in(idex_1_memtoreg_out),
    .New_PC_in(somador_1_z), .Zero_in(and_2_out), .ALUresult_in(alu_1_resultado),
    .read2_in(idex_1_read2_out), .Rd_in(idex_1_rd_out), .Jalr_ou_Jal_in(and_1_out),
    .Branch_out(exmem_1_branch_out), .MemWrite_out(exmem_1_memwrite_out), .MemRead_out(exmem_1_memread_out),
    .RegWrite_out(exmem_1_regwrite_out), .MemToReg_out(exmem_1_memtoreg_out),
    .New_PC_out(exmem_1_new_pc_out), .Zero_out(exmem_1_zero_out),
    .ALUresult_out({exmem_1_aluresult_out_2, exmem_1_aluresult_out}), .read2_out(exmem_1_read2_out),
    .Rd_out(exmem_1_rd_out), .Jalr_ou_Jal_out(exmem_1_jalr_ou_jal_out));
  and and_3 (and_3_out, exmem_1_branch_out, exmem_1_zero_out);
  or or_1 (or_1_out, and_3_out, exmem_1_jalr_ou_jal_out);
  RAM #(.addrWidth(24), .dataWidth(32)) ram_1 (
    .addr(exmem_1_aluresult_out), .we(exmem_1_memwrite_out), .oe(exmem_1_memread_out), .clk(clock_1_out),
    .din(exmem_1_read2_out), .dout(ram_1_dout));
  MEMWB memwb_1 (
    .CLK(clock_1_out), .RegWrite_in(exmem_1_regwrite_out), .MemToReg_in(exmem_1_memtoreg_out),
    .Mem_data_in(ram_1_dout), .ALUresult_in({exmem_1_aluresult_out_2, exmem_1_aluresult_out}),
    .Rd_in(exmem_1_rd_out), .RegWrite_out(memwb_1_regwrite_out), .MemToReg_out(memwb_1_memtoreg_out),
    .Mem_data_out(memwb_1_mem_data_out), .ALUresult_out(memwb_1_aluresult_out), .Rd_out(memwb_1_rd_out));
  Multiplexer #(.enable("false"), .width(32)) multiplexer_8 (
    .in0(memwb_1_aluresult_out), .in1(memwb_1_mem_data_out), .out(multiplexer_8_out),
    .sel(memwb_1_memtoreg_out));
endmodule

// VHDL entity ALU, as the project stores it:
library IEEE;
use IEEE.STD_LOGIC_1164.ALL;
use ieee.numeric_std.ALL;
use IEEE.std_logic_unsigned.ALL;

entity ALU is
    port(
    A, B       : in std_logic_vector(31 downto 0);   -- Operandos A e B de 32 bits da ALU
    controle   : in std_logic_vector(3 downto 0);    -- Entrada responsável por determinar a operação da ALU
    resultado  : out std_logic_vector(31 downto 0);  -- Resultado da operação feita pela ALU
    f_zero     : out std_logic;                      -- Flag indicadora de resultado igual a zero na operacão da ALU
    mode       : in std_logic;                       -- Modo de operação: 0 para operação única e 1 para operação vetorial
    vecSize     : in std_logic_vector(1 downto 0)     -- Tamanho do vetor de operações (usado no modo vetorial)
    );
end ALU;


architecture TypeArchitecture of ALU is

-- Declaração dos sinais temporários da ALU
signal resultado_nv : std_logic_vector(31 downto 0); -- Resultado não vetorial
signal resultado_v  : std_logic_vector(31 downto 0); -- Resultado vetorial
signal soma_v       : std_logic_vector(31 downto 0); -- Sinal temporário que armazena o resultado final da soma vetorial
signal sub_v        : std_logic_vector(31 downto 0); -- Sinal temporário que armazena o resultado final da subtração vetorial
signal shiftL_v     : std_logic_vector(31 downto 0); -- Sinal temporário que armazena o resultado final do Shift Left vetorial
signal shiftR_v     : std_logic_vector(31 downto 0); -- Sinal temporário que armazena o resultado final da Shift Right vetorial

signal A16_1 : std_logic_vector(15 downto 0);  -- Vetor que contém os bits de índice 31 até 16 do operando quando vecsize='10' (16 bits)
signal A16_2 : std_logic_vector(15 downto 0);  -- Vetor que contém os bits de índice 15 até 0 do operando quando vecsize='10' (16 bits)

signal A8_1 : std_logic_vector(7 downto 0);  -- Vetor que contém os bits de índice 31 até 24 do operando quando vecsize='01' (8 bits)
signal A8_2 : std_logic_vector(7 downto 0);  -- Vetor que contém os bits de índice 23 até 16 do operando quando vecsize='01' (8 bits)
signal A8_3 : std_logic_vector(7 downto 0);  -- Vetor que contém os bits de índice 15 até 8 do operando quando vecsize='01' (8 bits)
signal A8_4 : std_logic_vector(7 downto 0);  -- Vetor que contém os bits de índice 7 até 0 do operando quando vecsize='01' (8 bits)

signal A4_1 : std_logic_vector(3 downto 0);  -- Vetor que contém os bits de índice 31 até 28 do operando quando vecsize='00' (4 bits)
signal A4_2 : std_logic_vector(3 downto 0);  -- Vetor que contém os bits de índice 27 até 24 do operando quando vecsize='00' (4 bits)
signal A4_3 : std_logic_vector(3 downto 0);  -- Vetor que contém os bits de índice 23 até 20 do operando quando vecsize='00' (4 bits)
signal A4_4 : std_logic_vector(3 downto 0);  -- Vetor que contém os bits de índice 19 até 16 do operando quando vecsize='00' (4 bits)
signal A4_5 : std_logic_vector(3 downto 0);  -- Vetor que contém os bits de índice 15 até 12 do operando quando vecsize='00' (4 bits)
signal A4_6 : std_logic_vector(3 downto 0);  -- Vetor que contém os bits de índice 11 até 8 do operando quando vecsize='00' (4 bits)
signal A4_7 : std_logic_vector(3 downto 0);  -- Vetor que contém os bits de índice 7 até 4 do operando quando vecsize='00' (4 bits)
signal A4_8 : std_logic_vector(3 downto 0);  -- Vetor que contém os bits de índice 3 até 0 do operando quando vecsize='00' (4 bits)

signal integer_B : integer;                  -- Integer do valor binário que entra como operando B

begin

    -- Conversão da entrada B para integer para uso nas operações de deslocamento
    integer_B <= to_integer(unsigned(B));

    -- Divisão do sinal de entrada A em subvetores para as operações vetoriais
    A16_1 <= A(31 downto 16);
    A16_2 <= A(15 downto 0);

    A8_1 <= A(31 downto 24);
    A8_2 <= A(23 downto 16);
    A8_3 <= A(15 downto 8);
    A8_4 <= A(7 downto 0);

    A4_1 <= A(31 downto 28);
    A4_2 <= A(27 downto 24);
    A4_3 <= A(23 downto 20);
    A4_4 <= A(19 downto 16);
    A4_5 <= A(15 downto 12);
    A4_6 <= A(11 downto 8);
    A4_7 <= A(7 downto 4);
    A4_8 <= A(3 downto 0);
    
    
    -- Cálculos das operações vetoriais com base no tamanho do vetor (vecsize)
    soma_v <= (A + B) when vecSize = "11" else
             ((A16_1 + B(31 downto 16)) & (A16_2 + B(15 downto 0))) when vecSize = "10" else
             ((A8_1 + B(31 downto 24)) & (A8_2 + B(23 downto 16)) & (A8_3 + B(15 downto 8)) & (A8_4 + B(7 downto 0))) when vecSize = "01" else
             ((A4_1 + B(31 downto 28)) & (A4_2 + B(27 downto 24)) & (A4_3 + B(23 downto 20)) & (A4_4 + B(19 downto 16)) & (A4_5 + B(15 downto 12)) & (A4_6 + B(11 downto 8)) & (A4_7 + B(7 downto 4)) & (A4_8 + B(3 downto 0))) when vecSize = "00";
    
    sub_v <= (A - B) when vecSize = "11" else
             ((A16_1 - B(31 downto 16)) & (A16_2 - B(15 downto 0))) when vecSize = "10" else
             ((A8_1 - B(31 downto 24)) & (A8_2 - B(23 downto 16)) & (A8_3 - B(15 downto 8)) & (A8_4 - B(7 downto 0))) when vecSize = "01" else
             ((A4_1 - B(31 downto 28)) & (A4_2 - B(27 downto 24)) & (A4_3 - B(23 downto 20)) & (A4_4 - B(19 downto 16)) & (A4_5 - B(15 downto 12)) & (A4_6 - B(11 downto 8)) & (A4_7 - B(7 downto 4)) & (A4_8 - B(3 downto 0))) when vecSize = "00";
    
    -- Cálculos das operações de deslocamento vetoriais
    shiftL_v <= (std_logic_vector(shift_left(unsigned(A), integer_B))) when vecSize = "11" else
             ((std_logic_vector(shift_left(unsigned(A16_1), integer_B))) & std_logic_vector(shift_left(unsigned(A16_2), integer_B))) when vecSize = "10" else
             ((std_logic_vector(shift_left(unsigned(A8_1), integer_B))) & (std_logic_vector(shift_left(unsigned(A8_2), integer_B))) & (std_logic_vector(shift_left(unsigned(A8_3), integer_B))) & (std_logic_vector(shift_left(unsigned(A8_4), integer_B)))) when vecSize = "01" else
             ((std_logic_vector(shift_left(unsigned(A4_1), integer_B))) & (std_logic_vector(shift_left(unsigned(A4_2), integer_B))) & (std_logic_vector(shift_left(unsigned(A4_3), integer_B))) & (std_logic_vector(shift_left(unsigned(A4_4), integer_B))) & (std_logic_vector(shift_left(unsigned(A4_5), integer_B))) & (std_logic_vector(shift_left(unsigned(A4_6), integer_B))) & (std_logic_vector(shift_left(unsigned(A4_7), integer_B))) & (std_logic_vector(shift_left(unsigned(A4_8), integer_B)))) when vecSize = "00";

    shiftR_v <= (std_logic_vector(shift_right(unsigned(A), integer_B))) when vecSize = "11" else
             ((std_logic_vector(shift_right(unsigned(A16_1), integer_B))) & std_logic_vector(shift_right(unsigned(A16_2), integer_B))) when vecSize = "10" else
             ((std_logic_vector(shift_right(unsigned(A8_1), integer_B))) & (std_logic_vector(shift_right(unsigned(A8_2), integer_B))) & (std_logic_vector(shift_right(unsigned(A8_3), integer_B))) & (std_logic_vector(shift_right(unsigned(A8_4), integer_B)))) when vecSize = "01" else
             ((std_logic_vector(shift_right(unsigned(A4_1), integer_B))) & (std_logic_vector(shift_right(unsigned(A4_2), integer_B))) & (std_logic_vector(shift_right(unsigned(A4_3), integer_B))) & (std_logic_vector(shift_right(unsigned(A4_4), integer_B))) & (std_logic_vector(shift_right(unsigned(A4_5), integer_B))) & (std_logic_vector(shift_right(unsigned(A4_6), integer_B))) & (std_logic_vector(shift_right(unsigned(A4_7), integer_B))) & (std_logic_vector(shift_right(unsigned(A4_8), integer_B)))) when vecSize = "00";
    

    -- ALU vetorial (mode = 1) 
    resultado_v <= soma_v when controle = "0010" else
                sub_v when controle = "0110" else
                shiftL_v when controle = "0011" else
                shiftR_v when controle = "0111" else
                (others => '0');
    
    -- ALU não vetorial (mode = 0)
    resultado_nv <= (A + B) when controle = "0010" else
                   (A - B) when controle = "0110" else
                   (A XOR B) when controle = "0101" else
                   (A OR B) when controle = "0001" else
                   (A AND B) when controle = "0000" else
                   (std_logic_vector(shift_left(unsigned(A), integer_B))) when controle = "0011" else
                   (std_logic_vector(shift_right(unsigned(A), integer_B))) when controle = "0111";
    
    -- Seleção do resultado de acordo com o sinal de controle "mode"
    resultado <= resultado_nv when mode = '0' else
                resultado_v when mode = '1';
                
    -- Sinalização se o resultado é zero (serve para o Branch) -> como as operações vetoriais não incluem Branch, basta verificar do resultado não vetorial
    f_zero <= '1' when resultado_nv = "00000000000000000000000000000000" else '0';   

end TypeArchitecture;

// VHDL entity ALU_Control, as the project stores it:
library IEEE;
use IEEE.STD_LOGIC_1164.ALL;

entity ALU_Control is
    port(
        Funct7    		: IN std_logic_vector(6 downto 0);    	 -- Entrada do funct7
        Funct3    		: IN std_logic_vector(2 downto 0);    	 -- Entrada do funct3
        Opcode    		: IN std_logic_vector(6 downto 0);   	 -- Entrada do opcode
        AluOp   		: IN std_logic_vector(1 downto 0);       -- Entrada de códigos de operação da ALU (2 bits)
        ALU_Controle 	: OUT std_logic_vector(3 downto 0);      -- Saída do controle da ALU (4 bits)
        Beq_Bne		: OUT std_logic					 -- Sinal de controle para verificação de Beq ou Bne
        );
end ALU_Control;

architecture TypeArchitecture of ALU_Control is
begin

	ALU_Controle <= "0010" when AluOp = "00" else 	-- Operação de Load
			 	 "0110" when AluOp = "01" else 	-- Operação de Branch
			 	 "0010" when Funct7 = "0000000" and Funct3 = "000" else 	-- Operação de Soma
			 	 "0110" when Funct7 = "0100000" and Funct3 = "000" else 	-- Operação de Subtração
			 	 "0011" when Funct7 = "0000000" and Funct3 = "001" else 	-- Operação de Shift Left
			 	 "0101" when Funct7 = "0000000" and Funct3 = "100" else 	-- Operação XOR
			 	 "0111" when Funct7 = "0000000" and Funct3 = "101" else 	-- Operação de Shift Right
			 	 "0001" when Funct7 = "0000000" and Funct3 = "110" else 	-- Operação OR
			 	 "0000" when Funct7 = "0000000" and Funct3 = "111"; 		-- Operação AND
	Beq_Bne <= '1' when opcode="1100011" and Funct3="000" else '0';			-- '1' quando a instrução for Beq
	 
end TypeArchitecture;

// VHDL entity Control_Unit, as the project stores it:
library IEEE;
use IEEE.STD_LOGIC_1164.ALL;

entity Control_Unit is
    port(
        instruction                	: IN  std_logic_vector(31 downto 0);  -- Entrada da Instrução
        Stall                			: IN  std_logic;  				   -- Entrada do Hazard
        AluSrc, RegWrite, MemToReg 	: OUT std_logic;                      -- Sinais de Controle (1 Bit)
        MemRead, MemWrite, Branch  	: OUT std_logic;                      -- Sinais de Controle (1 Bit)
        Soma_PC 					: OUT std_logic;			   	   -- Sinais de Controle (1 Bit)	
        AluOp		               	: OUT std_logic_vector(1 downto 0);   -- Saída da Operação da ALU (2 Bits)
        S_funct7 					: OUT std_logic_vector(6 downto 0);   -- Saída do Funct7
        S_funct3 					: OUT std_logic_vector(2 downto 0);   -- Saída do Funct3
        S_opcode 					: OUT std_logic_vector(6 downto 0);   -- Saída do Opcode
        JumpReg					: OUT std_logic;				   -- Indica quando a instrução é jalr	
        mode						: OUT std_logic;				   -- Indica se é uma operação vetorial
        Vecsize					: OUT std_logic_vector(1 downto 0));  -- Indica o tamanho do vetor
        
end Control_Unit;

architecture TypeArchitecture of Control_Unit is

signal opcode : std_logic_vector(6 downto 0);	-- Opcode da Instrução
signal funct7 : std_logic_vector(6 downto 0);	-- Funct7 da Instrução
signal funct3 : std_logic_vector(2 downto 0);	-- Funct3 da Instrução


begin
	-- Definição do Opcode da Instrução
	opcode(0) <= instruction(0);
	opcode(1) <= instruction(1);
	opcode(2) <= instruction(2);
	opcode(3) <= instruction(3);
	opcode(4) <= instruction(4);
	opcode(5) <= instruction(5);
	opcode(6) <= instruction(6);
	Soma_PC <= '0'; 
	JumpReg <= '0';

	process(Stall)
	begin
		IF (Stall = '1') THEN
			AluSrc <= '0';
			RegWrite <= '0';
			MemToReg <= '0';
			MemRead <= '0';
			MemWrite <= '0';
			Branch <= '0';
			Soma_PC <= '0';
			JumpReg <= '0';
		end if; 
	end process;
	-- Definição das Funct7, Funct3 e dos Sinais de Controle de acordo com o opcode.
	process(opcode)
	begin
		IF (opcode = "0110011") THEN		-- R-Type Instruction
			funct7(6) <= instruction(31);
			funct7(5) <= instruction(30);
			funct7(4) <= instruction(29);
			funct7(3) <= instruction(28);
			funct7(2) <= instruction(27);
			funct7(1) <= instruction(26);
			funct7(0) <= instruction(25);
			funct3(2) <= instruction (14);
			funct3(1) <= instruction (13);
			funct3(0) <= instruction (12);
			AluSrc <= '0'; 			
			RegWrite <= '1';
			MemToReg <= '0';
			MemRead <= '0';
			MemWrite <= '0';
			Branch <= '0';
			mode <= '0';
			Vecsize <= "11";
			AluOp <= "10";
		END IF;
		IF (opcode = "0010011") THEN		-- I-Type Instruction (ADDi, ANDi, ORi, XORi, SLTi)
			funct7(6) <= '0';
			funct7(5) <= '0';
			funct7(4) <= '0';
			funct7(3) <= '0';
			funct7(2) <= '0';
			funct7(1) <= '0';
			funct7(0) <= '0';
			funct3(2) <= instruction (14);
			funct3(1) <= instruction (13);
			funct3(0) <= instruction (12);
			AluSrc <= '1'; 			
			RegWrite <= '1';
			MemToReg <= '0';
			MemRead <= '0';
			MemWrite <= '0';
			Branch <= '0';
			mode <= '0';
			Vecsize <= "11";
			AluOp <= "10";
		END IF;
		IF (opcode = "0000011") THEN		-- I-Type Instruction (Load)
			funct7(6) <= '0';
			funct7(5) <= '0';
			funct7(4) <= '0';
			funct7(3) <= '0';
			funct7(2) <= '0';
			funct7(1) <= '0';
			funct7(0) <= '0';
			funct3(2) <= '0';
			funct3(1) <= '0';
			funct3(0) <= '0';
			AluSrc <= '1'; 			
			RegWrite <= '1';
			MemToReg <= '1';
			MemRead <= '1';
			MemWrite <= '0';
			Branch <= '0';
			mode <= '0';
			Vecsize <= "11";
			AluOp <= "00";
		END IF;
		IF (opcode = "1100111") THEN		-- I-Type Instruction (Jump) 
			funct7(6) <= '0';
			funct7(5) <= '0';
			funct7(4) <= '0';
			funct7(3) <= '0';
			funct7(2) <= '0';
			funct7(1) <= '0';
			funct7(0) <= '0';
			funct3(2) <= '0';
			funct3(1) <= '0';
			funct3(0) <= '0';
			AluSrc <= '0'; 			
			RegWrite <= '0';
			MemToReg <= '0';
			MemRead <= '0';
			MemWrite <= '0';
			Branch <= '0';
			Soma_PC <= '1';
			JumpReg <= '1';
			mode <= '0';
			Vecsize <= "11";
			AluOp <= "01";
		END IF;
		IF (opcode = "0100011") THEN		-- S-Type Instruction 
			funct7(6) <= '0';
			funct7(5) <= '0';
			funct7(4) <= '0';
			funct7(3) <= '0';
			funct7(2) <= '0';
			funct7(1) <= '0';
			funct7(0) <= '0';
			funct3(2) <= '0';
			funct3(1) <= '0';
			funct3(0) <= '0';
			AluSrc <= '1'; 			
			RegWrite <= '0';
			MemToReg <= '0';
			MemRead <= '0';
			MemWrite <= '1';
			Branch <= '0';
			mode <= '0';
			Vecsize <= "11";
			AluOp <= "00";
		END IF;
		IF (opcode = "1101111") THEN		-- UJ-Type Instruction (jal)
			funct7(6) <= '0';
			funct7(5) <= '0';
			funct7(4) <= '0';
			funct7(3) <= '0';
			funct7(2) <= '0';
			funct7(1) <= '0';
			funct7(0) <= '0';
			funct3(2) <= '0';
			funct3(1) <= '0';
			funct3(0) <= '0';
			AluSrc <= '0'; 			
			RegWrite <= '1';
			MemToReg <= '0';
			MemRead <= '0';
			MemWrite <= '0';
			Branch <= '0';
			Soma_PC <= '1';
			mode <= '0';
			Vecsize <= "11";
			AluOp <= "10";
		END IF;
		IF (opcode = "0110111") THEN		-- U-Type Instruction (lui - soma com imediato muito grande)
			funct7(6) <= '0';
			funct7(5) <= '0';
			funct7(4) <= '0';
			funct7(3) <= '0';
			funct7(2) <= '0';
			funct7(1) <= '0';
			funct7(0) <= '0';
			funct3(2) <= '0';
			funct3(1) <= '0';
			funct3(0) <= '0';
			AluSrc <= '1'; 			
			RegWrite <= '1';
			MemToReg <= '0';
			MemRead <= '0';
			MemWrite <= '0';
			Branch <= '0';
			mode <= '0';
			Vecsize <= "11";
			AluOp <= "10";
		END IF;
		IF (opcode = "0010111") THEN		-- U-Type Instruction (auipc, soma do pc com o imediato e guarda no registrador)
			funct7(6) <= '0';
			funct7(5) <= '0';
			funct7(4) <= '0';
			funct7(3) <= '0';
			funct7(2) <= '0';
			funct7(1) <= '0';
			funct7(0) <= '0';
			funct3(2) <= '0';
			funct3(1) <= '0';
			funct3(0) <= '0';
			AluSrc <= '1'; 			
			RegWrite <= '1';
			MemToReg <= '0';
			MemRead <= '0';
			MemWrite <= '0';
			Branch <= '0';
			Soma_PC <= '1';
			mode <= '0';
			Vecsize <= "11";
			AluOp <= "10";
		END IF;
		IF (opcode = "1100011") THEN		-- Sb-Type Instruction 
			funct7(6) <= '0';
			funct7(5) <= '0';
			funct7(4) <= '0';
			funct7(3) <= '0';
			funct7(2) <= '0';
			funct7(1) <= '0';
			funct7(0) <= '0';
			funct3(2) <= instruction (14);
			funct3(1) <= instruction (13);
			funct3(0) <= instruction (12);
			AluSrc <= '0'; 			
			RegWrite <= '0';
			MemToReg <= '0';
			MemRead <= '0';
			MemWrite <= '0';
			Branch <= '1';
			mode <= '0';
			Vecsize <= "11";
			AluOp <= "01";
		END IF;
		IF (opcode = "1111100") 	THEN		-- R-Type Vetorial Instruction (4bits)
			funct7(6) <= instruction(31);
			funct7(5) <= instruction(30);
			funct7(4) <= instruction(29);
			funct7(3) <= instruction(28);
			funct7(2) <= instruction(27);
			funct7(1) <= instruction(26);
			funct7(0) <= instruction(25);
			funct3(2) <= instruction (14);
			funct3(1) <= instruction (13);
			funct3(0) <= instruction (12);
			AluSrc <= '0'; 			
			RegWrite <= '1';
			MemToReg <= '0';
			MemRead <= '0';
			MemWrite <= '0';
			Branch <= '0';
			mode <= '1';
			Vecsize <= "00";
			AluOp <= "10";
		END IF;
		IF (opcode = "1111101")  THEN				-- R-Type Vetorial Instruction (8bits)
			funct7(6) <= instruction(31);
			funct7(5) <= instruction(30);
			funct7(4) <= instruction(29);
			funct7(3) <= instruction(28);
			funct7(2) <= instruction(27);
			funct7(1) <= instruction(26);
			funct7(0) <= instruction(25);
			funct3(2) <= instruction (14);
			funct3(1) <= instruction (13);
			funct3(0) <= instruction (12);
			AluSrc <= '0'; 			
			RegWrite <= '1';
			MemToReg <= '0';
			MemRead <= '0';
			MemWrite <= '0';
			Branch <= '0';
			mode <= '1';
			Vecsize <= "01";
			AluOp <= "10";
		END IF;
		IF (opcode = "1111110")	THEN			-- R-Type Vetorial Instruction (16bits)
			funct7(6) <= instruction(31);
			funct7(5) <= instruction(30);
			funct7(4) <= instruction(29);
			funct7(3) <= instruction(28);
			funct7(2) <= instruction(27);
			funct7(1) <= instruction(26);
			funct7(0) <= instruction(25);
			funct3(2) <= instruction (14);
			funct3(1) <= instruction (13);
			funct3(0) <= instruction (12);
			AluSrc <= '0'; 			
			RegWrite <= '1';
			MemToReg <= '0';
			MemRead <= '0';
			MemWrite <= '0';
			Branch <= '0';
			mode <= '1';
			Vecsize <= "10";
			AluOp <= "10";
		END IF;
		IF (opcode = "1111000") THEN		-- I-Type Vetorial Instruction (Soma e deslocamento)(4bits)
			funct7(6) <= '0';
			funct7(5) <= '0';
			funct7(4) <= '0';
			funct7(3) <= '0';
			funct7(2) <= '0';
			funct7(1) <= '0';
			funct7(0) <= '0';
			funct3(2) <= instruction (14);
			funct3(1) <= instruction (13);
			funct3(0) <= instruction (12);
			AluSrc <= '1'; 			
			RegWrite <= '1';
			MemToReg <= '0';
			MemRead <= '0';
			MemWrite <= '0';
			Branch <= '0';
			mode <= '1';
			Vecsize <= "00";
			AluOp <= "10";
		END IF;
		IF (opcode = "1111001") THEN		-- I-Type Vetorial Instruction (Soma e deslocamento)(8bits)
			funct7(6) <= '0';
			funct7(5) <= '0';
			funct7(4) <= '0';
			funct7(3) <= '0';
			funct7(2) <= '0';
			funct7(1) <= '0';
			funct7(0) <= '0';
			funct3(2) <= instruction (14);
			funct3(1) <= instruction (13);
			funct3(0) <= instruction (12);
			AluSrc <= '1'; 			
			RegWrite <= '1';
			MemToReg <= '0';
			MemRead <= '0';
			MemWrite <= '0';
			Branch <= '0';
			mode <= '1';
			Vecsize <= "01";
			AluOp <= "10";
		END IF;
		IF (opcode = "1111010") THEN		-- I-Type Vetorial Instruction (Soma e deslocamento)(16bits)
			funct7(6) <= '0';
			funct7(5) <= '0';
			funct7(4) <= '0';
			funct7(3) <= '0';
			funct7(2) <= '0';
			funct7(1) <= '0';
			funct7(0) <= '0';
			funct3(2) <= instruction (14);
			funct3(1) <= instruction (13);
			funct3(0) <= instruction (12);
			AluSrc <= '1'; 			
			RegWrite <= '1';
			MemToReg <= '0';
			MemRead <= '0';
			MemWrite <= '0';
			Branch <= '0';
			mode <= '1';
			Vecsize <= "10";
			AluOp <= "10";
		END IF;
		IF (opcode = "1110000") THEN		-- U-Type Vetorial Instruction (4bits)(auipc)
			funct7(6) <= '0';
			funct7(5) <= '0';
			funct7(4) <= '0';
			funct7(3) <= '0';
			funct7(2) <= '0';
			funct7(1) <= '0';
			funct7(0) <= '0';
			funct3(2) <= '0';
			funct3(1) <= '0';
			funct3(0) <= '0';
			AluSrc <= '1'; 			
			RegWrite <= '1';
			MemToReg <= '0';
			MemRead <= '0';
			MemWrite <= '0';
			Branch <= '0';
			Soma_PC <= '1';
			mode <= '1';
			Vecsize <= "00";
			AluOp <= "10";
		END IF;
		IF (opcode = "1110001") THEN		-- U-Type Vetorial Instruction (4bits)(auipc)
			funct7(6) <= '0';
			funct7(5) <= '0';
			funct7(4) <= '0';
			funct7(3) <= '0';
			funct7(2) <= '0';
			funct7(1) <= '0';
			funct7(0) <= '0';
			funct3(2) <= '0';
			funct3(1) <= '0';
			funct3(0) <= '0';
			AluSrc <= '1'; 			
			RegWrite <= '1';
			MemToReg <= '0';
			MemRead <= '0';
			MemWrite <= '0';
			Branch <= '0';
			Soma_PC <= '1';
			mode <= '1';
			Vecsize <= "01";
			AluOp <= "10";
		END IF;
		IF (opcode = "1110010") THEN		-- U-Type Vetorial Instruction (4bits)(auipc)
			funct7(6) <= '0';
			funct7(5) <= '0';
			funct7(4) <= '0';
			funct7(3) <= '0';
			funct7(2) <= '0';
			funct7(1) <= '0';
			funct7(0) <= '0';
			funct3(2) <= '0';
			funct3(1) <= '0';
			funct3(0) <= '0';
			AluSrc <= '1'; 			
			RegWrite <= '1';
			MemToReg <= '0';
			MemRead <= '0';
			MemWrite <= '0';
			Branch <= '0';
			Soma_PC <= '1';
			mode <= '1';
			Vecsize <= "10";
			AluOp <= "10";
		END IF;
	end process;
	S_funct7 <= funct7;
	S_funct3 <= funct3;
	S_opcode <= opcode;
end TypeArchitecture;

// VHDL entity ImmGen, as the project stores it:
library IEEE;
use IEEE.STD_LOGIC_1164.ALL;
USE IEEE.NUMERIC_STD.ALL;

entity ImmGen is
    Port( 
        instruction: in std_logic_vector(31 downto 0);  	-- Entrada da Instrução 
        immediate: out std_logic_vector(31 downto 0)  		-- Saída do Valor Imediato
        );
end ImmGen;

architecture Behavioral of ImmGen is
    signal opcode       : std_logic_vector(6 downto 0);  		-- Sinal para armazenr o opcode da instrução
    signal S_imm  : std_logic_vector(31 downto 0) := "00000000000000000000000000000000";  -- Sinal auxiliar para definição do imediato

begin

    opcode <= instruction(6 downto 0);  -- Definição do opcode

    process(opcode)
    begin
        if (opcode = "0010011" or opcode = "0000011" or opcode = "1100111") then  	-- Tipo I 
            S_imm(11 downto 0)  <= instruction(31 downto 20);  					-- Seleciona o imediato 
            S_imm(31 downto 12) <= (others => instruction(31));  				-- Extensão do Bit de Sinal
        elsif (opcode = "1101111") then  									-- Tipo UJ 
            S_imm(20) <= instruction(31);  									-- Seleciona o imediato
            S_imm(10 downto 1) <= instruction(30 downto 21);					-- Seleciona o imediato
            S_imm(11) <= instruction(20);									-- Seleciona o imediato	
            S_imm(19 downto 12) <= instruction(19 downto 12);					-- Seleciona o imediato
            S_imm(31 downto 21) <= (others => instruction(31));					-- Extensão do Bit de Sinal
        elsif (opcode = "0110111" or opcode = "0010111") then										-- Tipo U 
        	  S_imm(31 downto 12) <= instruction(31 downto 12);  					-- Seleciona o imediato	
        elsif (opcode = "0100011") then  									-- Tipo S 
            S_imm(11 downto 5)  <= instruction(31 downto 25);  					-- Seleciona o imediato
            S_imm(4 downto 0)   <= instruction(11 downto 7);   					-- Seleciona o imediato
            S_imm(31 downto 12) <= (others => instruction(31));  				-- Extensão do Bit de Sinal
        elsif (opcode = "1100011") then  									-- Tipo SB
            S_imm(12)           <= instruction(31);          					-- Seleciona o imediato
            S_imm(11)           <= instruction(7);           					-- Seleciona o imediato
            S_imm(10 downto 5)  <= instruction(30 downto 25);  					-- Seleciona o imediato
            S_imm(4 downto 1)   <= instruction(11 downto 8);   					-- Seleciona o imediato
            S_imm(31 downto 13) <= (others => instruction(31));  				-- Extensão do Bit de Sinal
        end if;
    end process;

    immediate <= S_imm;  												-- Atribui o valor imeadiato à saída

end Behavioral;

// VHDL entity PC4, as the project stores it:
library IEEE;
use IEEE.STD_LOGIC_1164.ALL;
use ieee.numeric_std.ALL;
use IEEE.std_logic_unsigned.ALL;


ENTITY PC4 IS
  PORT (
    CLK      : IN  std_logic;                    		-- Entrada do Clock
    RESET    : IN  std_logic;                    		-- Entrada de Reset
    PC_in    : IN  std_logic_vector(31 DOWNTO 0); 	-- Entrada do endereço atual
    WriteEnable   : IN std_logic;               		-- Entrada de Habilitação de escrita no PC
    PC_out   : OUT std_logic_vector(31 DOWNTO 0)  	-- Saída do próximo endereço
    );
END PC4;

ARCHITECTURE TypeArchitecture OF PC4 IS

BEGIN

	PROCESS (CLK, RESET, WriteEnable)
	BEGIN
		IF (rising_edge(CLK)) THEN                      				-- Detecção do Clock
			if (PC_in = "UUUUUUUUUUUUUUUUUUUUUUUUUUUUUUUU") then   	-- Verificação de endereço indefinido
				PC_out <= (others => '0');               			-- Caso indefinido, início no primeiro endereço
			elsif (WriteEnable = '0') then              				-- WriteEnable desabilitado
				PC_out <= PC_in;								-- Manutenção do endereço atual
			elsif (WriteEnable = '1') then						-- WriteEnable habilitado
				PC_out <= PC_in + '1';							-- Atualização do endereço
			end if;
		END IF;
		IF (RESET = '1') THEN                           				-- Detecção de Reset
			PC_out <= (others => '0');                   			-- Retorno ao primeiro endereço
		END IF;
	END PROCESS;

END TypeArchitecture;

// VHDL entity Somador, as the project stores it:
LIBRARY ieee;
USE ieee.std_logic_1164.all;
USE IEEE.std_logic_unsigned.ALL; 

ENTITY Somador IS
  PORT (
    A, B        : IN  std_logic_vector(31 DOWNTO 0); 	-- Entrada de vetores de 32 bits
    Z           : OUT std_logic_vector(31 DOWNTO 0) 	-- Saída do vetor resultado da soma
    );
END Somador;

ARCHITECTURE TypeArchitecture OF somador IS

BEGIN

Z <= A + B; 									-- Vetor resultado da soma

END TypeArchitecture;

// VHDL entity RegisterFile, as the project stores it:
library ieee;
use ieee.std_logic_1164.all;
use ieee.numeric_std.all;

entity RegisterFile is
  port(
    ReadRegister_1           : in std_logic_vector(4 downto 0);    	-- Endereço do primeiro registrador a ser lido
    ReadRegister_2           : in std_logic_vector(4 downto 0);    	-- Endereço do segundo registrador a ser lido
    WriteRegister      	    : in std_logic_vector(4 downto 0);    	-- Endereço do registrador a ser escrito
    WriteData                : in  std_logic_vector(31 downto 0);     -- Dado a ser escrito
    RegWrite  			    : in  std_logic;     				-- Sinal de controle
    ReadData_1         	    : out  std_logic_vector(31 downto 0);    -- Dado do primeiro registrador lido
    ReadData_2       	    : out  std_logic_vector(31 downto 0);    -- Dado do segundo registrador lido
    CLK                 	    : in  std_logic                        	-- Sinal do CLOCK
    );
end RegisterFile;

architecture TypeArchitecture of RegisterFile is
  type RegisterFile is array(0 to 31) of std_logic_vector(31 downto 0);
  signal Registers : RegisterFile := 
   ("00000000000000000000000000000000","00000000000000000000000000000000","00000000000000000000000000000000","00000000000000000000000000000000",
    "00000000000000000000000000000000","00000000000000000000000000000000","00000000000000000000000000000000","00000000000000000000000000000000",
    "00000000000000000000000000000000","00000000000000000000000000000000","00000000000000000000000000000000","00000000000000000000000000000000",
    "00000000000000000000000000000000","00000000000000000000000000000000","00000000000000000000000000000000","00000000000000000000000000000000",
    "00000000000000000000000000000000","00000000000000000000000000000000","00000000000000000000000000000000","00000000000000000000000000000000",
    "00000000000000000000000000000000","00000000000000000000000000000000","00000000000000000000000000000000","00000000000000000000000000000000",
    "00000000000000000000000000000000","00000000000000000000000000000000","00000000000000000000000000000000","00000000000000000000000000000000",
    "00000000000000000000000000000000","00000000000000000000000000000000","00000000000000000000000000000000","00000000000000000000000000000000");

begin
  regFile : process (CLK) is
  begin
    if falling_edge(CLK) then
      if (Registers(to_integer(unsigned(ReadRegister_1))) = "UUUUUUUUUUUUUUUUUUUUUUUUUUUUUUUU") THEN -- Caso o valor do registrador esteja indefinido, a saída será "000..."
      	ReadData_1 <= (others => '0');  
      ELSE 
      	ReadData_1 <= registers(to_integer(unsigned(ReadRegister_1)));  -- Leitura do valor contido no registrador 1
      END IF;
      IF (Registers(to_integer(unsigned(ReadRegister_2))) = "UUUUUUUUUUUUUUUUUUUUUUUUUUUUUUUU") THEN -- Caso o valor do registrador esteja indefinido, a saída será "000..."
      	ReadData_2 <= (others => '0');  
      ELSE
      	ReadData_2 <= registers(to_integer(unsigned(ReadRegister_2)));  -- Leitura do valor contido no registrador 2 
      END IF;
    end if; 
    if rising_edge(CLK) then
      if RegWrite = '1' then
        Registers(to_integer(unsigned(WriteRegister))) <= WriteData;      -- Escrita do valor no registrador selecionado
      end if;
    end if;
  end process;
  
end TypeArchitecture;

// VHDL entity IFID, as the project stores it:
LIBRARY ieee;
USE ieee.std_logic_1164.all;

ENTITY IFID IS
  PORT (
    CLK         : IN  std_logic;                    -- Entrada do CLOCK
    PC_in        : IN  std_logic_vector(31 DOWNTO 0); -- Entrada do valor atual do PC (contador de programa)
    PC4_in	 : IN  std_logic_vector(31 downto 0); -- Entrada do valor do PC mais 4 (próxima instrução)
    WriteEnable   : IN std_logic;                 -- Entrada do sinal de habilitação de escrita no IFID
    Instruction_In      : IN  std_logic_vector(31 DOWNTO 0); -- Entrada da instrução atual buscada na memória de instruções
    PC_out       : OUT std_logic_vector(31 DOWNTO 0); -- Saída do valor atual do PC (contador de programa)
    PC4_out	 : OUT std_logic_vector(31 downto 0); -- Saída do valor do PC mais 4 (próxima instrução)
    Instruction_Out     : OUT std_logic_vector(31 DOWNTO 0);  -- Saída da instrução atual buscada na memória de instruções
    Rs1 : OUT std_logic_vector(4 DOWNTO 0);  -- Saída da instrução atual buscada na memória de instruções
    Rs2 : OUT std_logic_vector(4 DOWNTO 0);  -- Saída da instrução atual buscada na memória de instruções
    Rd : OUT std_logic_vector(4 DOWNTO 0)  -- Saída da instrução atual buscada na memória de instruções
    );
END IFID;


ARCHITECTURE TypeArchitecture OF IFID IS

signal opcode : std_logic_vector(6 downto 0);	-- Opcode da Instrução
signal s_Rs1 : std_logic_vector(4 downto 0);		-- Rs1 da Instrução
signal s_Rs2 : std_logic_vector(4 downto 0);		-- Rs2 da Instrução
signal s_Rd : std_logic_vector(4 downto 0);		-- Rd da Instrução
SIGNAL IDIF : std_logic_vector(117 DOWNTO 0);  	-- Registrador de 96 bits para armazenar os valores do IFID

BEGIN
	-- Definição do Opcode da Instrução
	opcode(0) <= Instruction_In(0);
	opcode(1) <= Instruction_In(1);
	opcode(2) <= Instruction_In(2);
	opcode(3) <= Instruction_In(3);
	opcode(4) <= Instruction_In(4);
	opcode(5) <= Instruction_In(5);
	opcode(6) <= Instruction_In(6);

	process(opcode)
	begin
	-- Rs1
		IF NOT (opcode = "1101111" or opcode = "0110111") THEN  -- Tipos diferentes de U e UJ tem Rs1
		s_Rs1 (0) <= Instruction_In(15);
		s_Rs1 (1) <= Instruction_In(16);
		s_Rs1 (2) <= Instruction_In(17);
		s_Rs1 (3) <= Instruction_In(18);
		s_Rs1 (4) <= Instruction_In(19);
		END IF;

	-- Rs2
		IF (opcode = "0110011" or opcode = "0100011" or opcode = "1100011") THEN  -- Tipos R, S e Sb tem Rs2
		s_Rs2 (0) <= Instruction_In(20);
		s_Rs2 (1) <= Instruction_In(21);
		s_Rs2 (2) <= Instruction_In(22);
		s_Rs2 (3) <= Instruction_In(23);
		s_Rs2 (4) <= Instruction_In(24);
		END IF;

	-- Rd
		IF NOT (opcode = "0100011" or opcode = "1100011") THEN  -- Tipos diferentes de S e Sb tem Rd
		s_Rd (0) <= Instruction_In(7); 
		s_Rd (1) <= Instruction_In(8);
		s_Rd (2) <= Instruction_In(9);
		s_Rd (3) <= Instruction_In(10);
		s_Rd (4) <= Instruction_In(11);
		END IF;
	end process;

	
	PROCESS (CLK, WriteEnable)
	BEGIN
		IF (rising_edge(CLK)) THEN                   	-- Detecção de subida de CLOCK
			if (WriteEnable = '1') then             	-- Vericação se o WriteEnable está habilitado
				IDIF(31 DOWNTO 0) <= Instruction_In;       
				IDIF(63 DOWNTO 32) <= PC_in;          	-- Armazena o valor atual do PC
				IDIF(95 downto 64) <= PC4_in;       	-- Armazena o valor do PC mais 4 (próxima instrução)
				IDIF(102 downto 96) <= opcode;		-- Armazena o opcode
				IDIF(107 downto 103) <= s_Rs1;		-- Armazena o Rs1
				IDIF(112 downto 108) <= s_Rs2;		-- Armazena o Rs2
				IDIF(117 downto 113) <= s_Rd;			-- Armazena o Rd
			end if;
		END IF;
		IF (falling_edge(CLK)) THEN                 		-- Detecção de descida de CLOCK
			PC_out <= IDIF(63 DOWNTO 32);           	-- Definição do PC atual
			Instruction_Out <= IDIF(31 DOWNTO 0);        -- Definição da instrução armazenada
			PC4_out <= IDIF(95 downto 64);        		-- Saída de PC+4
			Rs1 <= IDIF(107 downto 103);				-- Saída do Rs1
			Rs2 <= IDIF(112 downto 108);				-- Saída do Rs2
			Rd <= IDIF(117 downto 113);				-- Saída do Rd
		END IF;
	END PROCESS;
	
END TypeArchitecture;

// VHDL entity IDEX, as the project stores it:
LIBRARY ieee;
USE ieee.std_logic_1164.all;

ENTITY IDEX IS
  PORT (
    CLK             : IN std_logic;                             -- Entrada do sinal de clock            
    ALUSrc_in       : IN std_logic;                             -- Entradas do ALUSrc e ALUOp, que são sinais de controle para a ALU_Control
    ALUOp_in        : IN std_logic_vector(1 downto 0);          -- ALUSrc e ALUOp são usados no estágio EX do pipeline, então não aparecem nos proximos regs do pipeline
    funct3_in       : IN std_logic_vector(2 downto 0);          -- Entrada do Funct3, usado na ALU_Control
    funct7_in       : IN std_logic_vector(6 downto 0);          -- Entrada do Funct7, usado na ALU_Control
    PC_in           : IN std_logic_vector(31 DOWNTO 0);         -- Entrada do valor atual do PC (contador de programa)
    Soma_PC_in      : IN std_logic;                             -- Entrada do sinal de controle que define quando o PC deve ser somado (jal)        
    Branch_in       : IN std_logic;                             -- Entrada do sinal de controle que define quando ocorre Branch
    MemWrite_in     : IN std_logic;                             -- Entrada do sinal de controle que define quando a Memória será escrita
    MemRead_in      : IN std_logic;                             -- Entrada do sinal de controle que define quando a Memória será lida
    RegWrite_in     : IN std_logic;                             -- Entrada do sinal de controle que define quando o registrador será escrito
    MemToReg_in     : IN std_logic;                             -- Entrada do sinal de controle que define quando um dado será passado da memória para o registrador
    read1_in        : IN std_logic_vector(31 DOWNTO 0);         -- Entrada do valor lido do read data 1
    read2_in        : IN std_logic_vector(31 DOWNTO 0);         -- Entrada do valor lido do read data 2
    immediate_in    : in std_logic_vector(31 DOWNTO 0);         -- Entrada do imediato gerado pelo ImmGen
    Rd_in           : IN std_logic_vector(4 DOWNTO 0);          -- Entrada da instrução atual buscada na memória de instruções
    Opcode_in       : IN std_logic_vector(6 DOWNTO 0);          -- Entrada do Opcode
    JumpReg_in      : IN std_Logic;                             -- Entrada do JumpReg
    Rs1_In          : IN std_logic_vector(4 downto 0);          -- Entrada do Rs1   
    Rs2_In          : IN std_logic_vector(4 downto 0);          -- Entrada do Rs2
    mode_in         : in std_logic;                             -- Modo de operação: 0 para operação única e 1 para operação vetorial
    vecsize_in      : in std_logic_vector(1 downto 0);          -- Tamanho do vetor de operações (usado no modo vetorial)
  
    ALUSrc_out      : out std_logic;                            -- Saídas do ALUSrc e ALUOp, que são sinais de controle para a ALU_Control
    ALUOp_out       : out std_logic_vector(1 downto 0);         -- ALUSrc e ALUOp são usados no estágio EX do pipeline, então não aparecem nos proximos regs do pipeline
    funct3_out      : out std_logic_vector(2 downto 0);         -- Saída do Funct3, usado na ALU_Control    
    funct7_out      : out std_logic_vector(6 downto 0);         -- Saída do Funct7, usado na ALU_Control
    PC_out          : out std_logic_vector(31 DOWNTO 0);        -- Saída do valor atual do PC (contador de programa)
    Soma_PC_out     : out std_logic;                            -- Saída do sinal de controle que define quando o PC deve ser somado (jal)
    Branch_out      : out std_logic;                            -- Saída do sinal de controle que define quando ocorre Branch
    MemWrite_out    : out std_logic;                            -- Saída do sinal de controle que define quando a Memória será escrita
    MemRead_out     : out std_logic;                            -- Saída do sinal de controle que define quando a Memória será lida
    RegWrite_out    : out std_logic;                            -- Saída do sinal de controle que define quando o registrador será escrito
    MemToReg_out    : out std_logic;                            -- Saída do sinal de controle que define quando um dado será passado da memória para o registrador
    read1_out       : out std_logic_vector(31 DOWNTO 0);        -- Saída do valor lido do read data 1
    read2_out       : out std_logic_vector(31 DOWNTO 0);        -- Saída do valor lido do read data 2   
    immediate_out   : out std_logic_vector(31 DOWNTO 0);        -- Saída do imediato gerado pelo ImmGen
    Rd_out          : out std_logic_vector(4 DOWNTO 0);         -- Saída da instrução atual buscada na memória de instruções
    Opcode_out      : out std_logic_vector(6 DOWNTO 0);         -- Saída do Opcode
    JumpReg_out     : out std_Logic;                            -- Saída do JumpReg
    Rs1_out         : out std_logic_vector(4 downto 0);         -- Saída do Rs1 
    Rs2_out         : out std_logic_vector(4 downto 0);          -- Saída do Rs2
    mode_out        : out std_logic;                            -- Modo de operação: 0 para operação única e 1 para operação vetorial
    vecsize_out     : out std_logic_vector(1 downto 0)          -- Tamanho do vetor de operações (usado no modo vetorial)
    );  
END IDEX;


ARCHITECTURE TypeArchitecture OF IDEX IS

SIGNAL idex_sig : std_logic_vector(173 DOWNTO 0);  -- Registrador de 151 bits para armazenar os valores do IDEX

BEGIN

    PROCESS (CLK)
    BEGIN
        IF (rising_edge(CLK)) THEN                   -- Detecção de subida de CLOCK
            idex_sig(0) <= ALUSrc_in;          
            idex_sig(2 downto 1) <= ALUOp_in;          
            idex_sig(5 DOWNTO 3) <= funct3_in;      
            idex_sig(12 DOWNTO 6) <= funct7_in;
            idex_sig(44 DOWNTO 13) <= PC_in ;  
            idex_sig(45) <= Soma_PC_in;       
            idex_sig(46) <= Branch_in;   
            idex_sig(47) <= MemWrite_in;   
            idex_sig(48) <= MemRead_in;   
            idex_sig(49) <= RegWrite_in;   
            idex_sig(50) <= MemToReg_in;   
            idex_sig(82 DOWNTO 51) <= read1_in;    
            idex_sig(114 DOWNTO 83) <= read2_in;    
            idex_sig(146 DOWNTO 115) <= immediate_in;   
            idex_sig(152 DOWNTO 147) <= Rd_in;
            idex_sig(159 downto 153) <= Opcode_in; 
            idex_sig(160) <= JumpReg_in;  
            idex_sig(165 downto 161) <= Rs1_In;
            idex_sig(170 downto 166) <= Rs2_In;
            idex_sig(171) <= mode_in;        
            idex_sig(173 downto 172) <= vecsize_in;   
        END IF;
        IF (falling_edge(CLK)) THEN                 -- Detecção de descida de CLOCK
            ALUSrc_out <= idex_sig(0);       
            ALUOp_out  <= idex_sig(2 downto 1);     
            funct3_out <= idex_sig(5 DOWNTO 3);      
            funct7_out <= idex_sig(12 DOWNTO 6);    
            PC_out <= idex_sig(44 DOWNTO 13);
            Soma_PC_out <= idex_sig(45);
            Branch_out <= idex_sig(46);
            MemWrite_out <= idex_sig(47);
            MemRead_out <= idex_sig(48);
            RegWrite_out <= idex_sig(49);
            MemToReg_out <= idex_sig(50);
            read1_out <= idex_sig(82 DOWNTO 51);
            read2_out <= idex_sig(114 DOWNTO 83);
            immediate_out <= idex_sig(146 DOWNTO 115);
            Rd_out <= idex_sig(152 DOWNTO 147);
            Opcode_out <= idex_sig(159 downto 153);
            JumpReg_out <= idex_sig(160);
            Rs1_out <= idex_sig(165 downto 161);
            Rs2_out <= idex_sig(170 downto 166);
            mode_out <= idex_sig(171);
            vecsize_out <= idex_sig(173 downto 172);
            
        END IF;
    END PROCESS;

    
END TypeArchitecture;

// VHDL entity EXMEM, as the project stores it:
LIBRARY ieee;
USE ieee.std_logic_1164.all;

ENTITY EXMEM IS
  PORT (
    CLK             : IN std_logic;                             -- Entrada do sinal de clock            
    Branch_in       : IN std_logic;                             -- Entrada do sinal de controle que define quando ocorre Branch
    MemWrite_in     : IN std_logic;                             -- Entrada do sinal de controle que define quando a Memória será escrita
    MemRead_in      : IN std_logic;                             -- Entrada do sinal de controle que define quando a Memória será lida
    RegWrite_in     : IN std_logic;                             -- Entrada do sinal de controle que define quando o registrador será escrito
    MemToReg_in     : IN std_logic;                             -- Entrada do sinal de controle que define quando um dado será passado da memória para o registrador
    New_PC_in       : IN std_logic_vector(31 DOWNTO 0);         -- Soma do PC com imediato (jal) ou reg com imediato substituindo PC (jalr)
    Zero_in         : IN std_logic;                             -- Quando o resultado da ALU foi zero (serve para Branch)
    ALUresult_in    : IN std_logic_vector(31 DOWNTO 0);         -- Entrada do resultado da operação da ALU
    read2_in        : IN std_logic_vector(31 DOWNTO 0);         -- Entrada do valor lido do read data 2
    Rd_in           : IN std_logic_vector(4 DOWNTO 0);          -- Entrada da instrução atual buscada na memória de instruções
    Jalr_ou_Jal_in	: IN std_logic;					    -- Entrada que indica se é Jalr ou Jal	
  
    Branch_out      : out std_logic;                            -- Saída do sinal de controle que define quando ocorre Branch 
    MemWrite_out    : out std_logic;                            -- Saída do sinal de controle que define quando a Memória será escrita
    MemRead_out     : out std_logic;                            -- Saída do sinal de controle que define quando a Memória será lida
    RegWrite_out    : out std_logic;                            -- Saída do sinal de controle que define quando o registrador será escrito
    MemToReg_out    : out std_logic;                            -- Saída do sinal de controle que define quando um dado será passado da memória para o registrador
    New_PC_out       : out std_logic_vector(31 DOWNTO 0);        -- Soma do PC com imediato (jal) ou reg com imediato substituindo PC (jalr)
    Zero_out        : out std_logic;                            -- Quando o resultado da ALU foi zero (serve para Branch)
    ALUresult_out   : out std_logic_vector(31 DOWNTO 0);        -- Saída do resultado da operação da ALU
    read2_out       : out std_logic_vector(31 DOWNTO 0);        -- Saída do valor lido do read data 2
    Rd_out          : out std_logic_vector(4 DOWNTO 0);          -- Saída da instrução atual buscada na memória de instruções
    Jalr_ou_Jal_out	: out std_logic					    -- Saída que indica se é Jalr ou Jal
    );
END EXMEM;


ARCHITECTURE TypeArchitecture OF EXMEM IS

SIGNAL exmem_sig : std_logic_vector(107 DOWNTO 0);  -- Registrador de 192 bits para armazenar os valores do EXMEM

BEGIN

    PROCESS (CLK)
    BEGIN
        IF (rising_edge(CLK)) THEN                   -- Detecta a borda de subida do sinal de clock
            exmem_sig(0)    <= Branch_in;          
            exmem_sig(1)    <= MemWrite_in;          
            exmem_sig(2)   <= MemRead_in;      
            exmem_sig(3)   <= RegWrite_in;
            exmem_sig(4)   <= MemToReg_in;  
            exmem_sig(36 downto 5)    <= New_PC_in;       
            exmem_sig(37)           <= Zero_in;   
            exmem_sig(69 downto 38)    <= ALUresult_in;   
            exmem_sig(101 downto 70)    <= read2_in;   
            exmem_sig(106 downto 102)    <= Rd_in;   
            exmem_sig(107) <= Jalr_ou_Jal_in;
        END IF;
        IF (falling_edge(CLK)) THEN                 -- Detecta a borda de descida do sinal de clock
            Branch_out    <= exmem_sig(0);       
            MemWrite_out  <= exmem_sig(1);     
            MemRead_out  <= exmem_sig(2);      
            RegWrite_out <= exmem_sig(3);    
            MemToReg_out <= exmem_sig(4);
            New_PC_out <= exmem_sig(36 downto 5);
            Zero_out <= exmem_sig(37);
            ALUresult_out <= exmem_sig(69 downto 38);
            read2_out <= exmem_sig(101 downto 70);
            Rd_out <= exmem_sig(106 downto 102);
            Jalr_ou_Jal_out <= exmem_sig(107);
        END IF;
    END PROCESS;

    
END TypeArchitecture;

// VHDL entity Hazard, as the project stores it:
library IEEE;
use IEEE.STD_LOGIC_1164.ALL;

entity Hazard is 
    port( 
        clk                 : IN std_logic;                          -- Entrada do sinal de clock
        MemRead_in          : IN std_logic;                          -- Sinal de controle que define quando a Memória será lida
        Rd_EX               : IN std_logic_vector(4 downto 0);       -- Rd é o endereço de destino da operação feita pelo CPU após o estágio de EX
        Rs1, Rs2            : IN std_logic_vector(4 downto 0);       -- Rs1 e Rs2 são os endereços dos registradores contidos na instrução
        stall               : OUT std_logic                          -- Saída que indica se um "stall" (atraso) deve ser aplicado no pipeline
    );
end Hazard;

architecture Behavioral of Hazard is

    signal stall_interno : std_logic := '0';  -- Signal temporário que armazena o nível lógico do stall

begin
    process(clk)
    begin
        if ((MemRead_in = '1') and ((Rd_EX = Rs1) or (Rd_EX = Rs2))) then        -- Fórmula do livro, página 322
            stall_interno <= '1';                                                -- Se o sinal de controle de MemRead_in for igual a 1 e o resultado  
        end if;                                                                  -- do estágio de Execution estiver em Rs1 ou Rs2, realiza um stall
    end process;

    stall <= stall_interno;                                                     -- Atribui o valor do signal temporário stall_interno à saída stall

end Behavioral;

// VHDL entity Forward, as the project stores it:
library IEEE;
use IEEE.STD_LOGIC_1164.ALL;

entity Forward is 
    port( 
         clk                        : IN std_logic;                         -- Entrada do sinal de clock
         regWrite_WB, regWrite_MEM  : IN std_logic;                         -- Sinais de controle de escrita no registrador do WB e do Mem, respectivamente
         Rs1, Rs2                   : IN std_logic_vector(4 downto 0);      -- Endereçoes dos registradores Rs1 e Rs2 vindos do estágio ID/EX do pipeline
         Rd_WB, Rd_Mem              : IN std_logic_vector(4 downto 0);      -- Endereços dos registradores de armazenamento Rd, vindos dos estágios de MEM/WB e EX/MEM do pipeline
         forwardA, forwardB         : OUT std_logic_vector(1 downto 0)      -- Saídas indicando os forwards para as fontes A e B
     );
end Forward;

ARCHITECTURE TypeArchitecture OF MEMWB IS
    signal forwardA_interno, forwardB_interno : std_logic_vector(1 downto 0) := "00";   -- Sinais internos que armazenam o encaminhamento

begin
    process(clk)
    begin
        if ((regWrite_MEM = '1') and (not(Rd_Mem = "00000")) and (Rd_Mem = Rs1)) then
            forwardA_interno <= "10";   
        end if;

        if ((regWrite_MEM = '1') and (not(Rd_Mem = "00000")) and (Rd_Mem = Rs2)) then
            forwardB_interno <= "10";  
        end if;

        if ((regWrite_WB = '1') and (not(Rd_WB = "00000")) and (Rd_WB = Rs1)) then
            forwardA_interno <= "01";   
        end if;

        if ((regWrite_WB = '1') and (not(Rd_WB = "00000")) and (Rd_WB = Rs2)) then
            forwardB_interno <= "01";   
        end if;

    end process;

    forwardA <= forwardA_interno;  
    forwardB <= forwardB_interno;
       
END TypeArchitecture;

// VHDL entity MEMWB, as the project stores it:
LIBRARY ieee;
USE ieee.std_logic_1164.all;

ENTITY MEMWB IS
  PORT (
    CLK             : IN std_logic;                             -- Entrada do sinal de clock            
    RegWrite_in     : IN std_logic;                             -- Entrada do sinal de controle que define quando o registrador será escrito
    MemToReg_in     : IN std_logic;                             -- Entrada do sinal de controle que define quando um dado será passado da memória para o registrador
    Mem_data_in     : IN std_logic_vector(31 DOWNTO 0);         -- Entrada do valor lido na memória
    ALUresult_in    : IN std_logic_vector(31 DOWNTO 0);         -- Entrada do resultado da operação da ALU
    Rd_in           : IN std_logic_vector(4 DOWNTO 0);          -- Entrada da instrução atual buscada na memória de instruções
  
    RegWrite_out    : out std_logic;                            -- Saída do sinal de controle que define quando o registrador será escrito
    MemToReg_out    : out std_logic;                            -- Saída do sinal de controle que define quando um dado será passado da memória para o registrador
    Mem_data_out    : out std_logic_vector(31 DOWNTO 0);        -- Saída do valor lido na memória
    ALUresult_out   : out std_logic_vector(31 DOWNTO 0);        -- Saída do resultado da operação da ALU
    Rd_out          : out std_logic_vector(4 DOWNTO 0)          -- Saída da instrução atual buscada na memória de instruções
    );
END MEMWB;


ARCHITECTURE TypeArchitecture OF MEMWB IS

SIGNAL memwb_sig : std_logic_vector(70 DOWNTO 0);  -- Registrador de 70 bits para armazenar os valores do memwb

BEGIN

    PROCESS (CLK)
    BEGIN
        IF (rising_edge(CLK)) THEN                   -- Detecta a borda de subida do sinal de clock     
            memwb_sig(0)   <= RegWrite_in;
            memwb_sig(1)   <= MemToReg_in;  
            memwb_sig(33 downto 2)  <= Mem_data_in ;       
            memwb_sig(65 downto 34)  <= ALUresult_in;   
            memwb_sig(70 downto 66)  <= Rd_in;   
        END IF;
        IF (falling_edge(CLK)) THEN                 -- Detecta a borda de descida do sinal de clock
            RegWrite_out <= memwb_sig(0);    
            MemToReg_out <= memwb_sig(1);
            Mem_data_out <= memwb_sig(33 downto 2);
            ALUresult_out <= memwb_sig(65 downto 34);
            Rd_out <= memwb_sig(70 downto 66);
        END IF;
    END PROCESS;

    
END TypeArchitecture;
